# Fritzing sketch circuit_diagram (saved by Fritzing 0.9.2b)
breadboards: 1

parts:
  Arduino = Arduino Uno (Rev3)
  Solenoid = Solenoid
  Center_Limit_Switch = SWITCH-MOMENTARY-2 [package=reed_switch_plastic]
  Rotation_Limit_Switch = SWITCH-MOMENTARY-2 [package=reed_switch_plastic]
  IR_Reflectance_Sensor = QRD1114 [package=qrd1114]
  Transistor = NPN-Transistor [part_number=TIP31C package="TO92 [THT]"]
  Diode = Diode [part_number=1N5408 package=diode-hv]
  Power = DC Power [voltage=12V]
  R1 = Resistor [tolerance=±5% resistance=200 package="2010 [SMD]"]
  R2 = Resistor [tolerance=±5% resistance=10k package="2010 [SMD]"]
  R3 = Resistor [tolerance=±5% resistance=127 package="0402 [SMD]"]

nets:
  N1: Arduino.D10_PWM/SS, R3.Pin_0
  N2: Arduino.D11_PWM/MOSI, Center_Limit_Switch.1
  GND: Arduino.GND, Center_Limit_Switch.2, Rotation_Limit_Switch.2, IR_Reflectance_Sensor.C, IR_Reflectance_Sensor.K, Transistor.E, Power.V-
  N3: Arduino.A5/SCL, IR_Reflectance_Sensor.E, R2.Pin_0
  N4: Arduino.D7, Rotation_Limit_Switch.1
  N5: Arduino.5V, R1.Pin_1, R2.Pin_1
  N6: Solenoid.pin1, Transistor.C, Diode.A
  N7: Solenoid.pin2, Diode.C, Power.V+
  N8: IR_Reflectance_Sensor.A, R1.Pin_0
  N9: Transistor.B, R3.Pin_1
